// Logisim project cache.circ as structural Verilog: 2 circuits, main circuit cache-entry
module main (
  input  [7:0] address,
  input  read_enable,
  input  [31:0] ROM_data_in,
  output [7:0] data_out,
  output [5:0] ROM_read_address,
  output ROM_read_enable
);

  wire and_1_out, cache_entry_1_miss, cache_entry_2_miss, cache_entry_3_miss, cache_entry_4_miss,
       demultiplexer_1_out0, demultiplexer_1_out1, demultiplexer_1_out2, demultiplexer_1_out3;
  wire [7:0] multiplexer_3_out, multiplexer_4_out;
  wire [31:0] cache_entry_1_data_out, cache_entry_2_data_out, cache_entry_3_data_out, cache_entry_4_data_out,
       multiplexer_1_out;

  Demultiplexer #(.select(2), .enable("false")) demultiplexer_1 (
    .out0(demultiplexer_1_out0), .out1(demultiplexer_1_out1), .out2(demultiplexer_1_out2),
    .out3(demultiplexer_1_out3), .in(and_1_out), .sel(address[3:2]));
  and and_1 (and_1_out, ROM_read_enable, ~read_enable);  // AND_Gate
  cache_entry cache_entry_1 (
    .tag(address[7:4]), .clock(demultiplexer_1_out0), .data_out(cache_entry_1_data_out),
    .miss(cache_entry_1_miss), .data_in(ROM_data_in));
  cache_entry cache_entry_2 (
    .tag(address[7:4]), .clock(demultiplexer_1_out1), .data_out(cache_entry_2_data_out),
    .miss(cache_entry_2_miss), .data_in(ROM_data_in));
  cache_entry cache_entry_3 (
    .tag(address[7:4]), .clock(demultiplexer_1_out2), .data_out(cache_entry_3_data_out),
    .miss(cache_entry_3_miss), .data_in(ROM_data_in));
  cache_entry cache_entry_4 (
    .tag(address[7:4]), .clock(demultiplexer_1_out3), .data_out(cache_entry_4_data_out),
    .miss(cache_entry_4_miss), .data_in(ROM_data_in));
  Multiplexer #(.select(2), .width(32), .enable("false")) multiplexer_1 (
    .in0(cache_entry_1_data_out), .in1(cache_entry_2_data_out), .in2(cache_entry_3_data_out),
    .in3(cache_entry_4_data_out), .out(multiplexer_1_out), .sel(address[3:2]));
  Multiplexer #(.select(2), .enable("false")) multiplexer_2 (
    .in0(cache_entry_1_miss), .in1(cache_entry_2_miss), .in2(cache_entry_3_miss), .in3(cache_entry_4_miss),
    .out(ROM_read_enable), .sel(address[3:2]));
  Multiplexer #(.select(2), .width(8), .enable("false")) multiplexer_3 (
    .in0(multiplexer_1_out[7:0]), .in1(multiplexer_1_out[15:8]), .in2(multiplexer_1_out[23:16]),
    .in3(multiplexer_1_out[31:24]), .out(multiplexer_3_out), .sel(address[1:0]));
  Multiplexer #(.select(2), .width(8), .enable("false")) multiplexer_4 (
    .in0(ROM_data_in[7:0]), .in1(ROM_data_in[15:8]), .in2(ROM_data_in[23:16]), .in3(ROM_data_in[31:24]),
    .out(multiplexer_4_out), .sel(address[1:0]));
  Multiplexer #(.width(8), .enable("false")) multiplexer_5 (
    .in0(multiplexer_3_out), .in1(multiplexer_4_out), .out(data_out), .sel(ROM_read_enable));

  assign ROM_read_address = address[7:2];

  // Notes on the sheet:
  //   data_out: pull=down
  //   ROM_read_address: pull=down
  //   ROM_read_enable: pull=down
endmodule

module cache_entry (
  input  [31:0] data_in,
  input  [3:0] tag,
  input  clock,
  output [31:0] data_out,
  output miss
);

  wire comparator_1_eq, valid_bit_q;
  wire [3:0] current_tag_q;

  Register #(.width(4)) current_tag (.D(tag), .en(miss), .Q(current_tag_q), .clk(clock));  // open: clr
  Comparator #(.width(4)) comparator_1 (.a(tag), .b(current_tag_q), .eq(comparator_1_eq));  // open: gt, lt
  Register #(.width(32)) cache_line (.D(data_in), .en(miss), .Q(data_out), .clk(clock));  // open: clr
  Register #(.width(1)) valid_bit (.D(1'b1), .en(miss), .Q(valid_bit_q), .clk(clock));  // open: clr
  nand nand_1 (miss, comparator_1_eq, valid_bit_q);
endmodule
